# Fritzing sketch hookup_diagram (saved by Fritzing 0.8.7b)
breadboards: 1

parts:
  BeagleBone1 = BeagleBone Black
  R2 = Resistor [tolerance=±5% resistance=2 package=THT]
  PIR1 = PIR sensor

nets:
  N1: BeagleBone1.no_name_yet#1, PIR1.SIG
  N2: BeagleBone1.no_name_yet#8, R2.Pin_0, PIR1.VDD
  N3: BeagleBone1.no_name_yet#12, R2.Pin_1, PIR1.GND

custom parts:
  BeagleBone Black: BeagleBone Black rev. A5B
